# Fritzing sketch SchemaFritzing (saved by Fritzing 0.9.3b)
breadboards: 1

parts:
  Componente1 = Arduino Uno (Rev3)
  R1 = Rotary Potentiometer (Small) [maximum_resistance=100kΩ package=THT]  # not connected
  LED1 = LED - 5mm [color="Red (633nm)" package="5 mm [THT]"]
  LED2 = LED - 5mm [color="Green (560nm)" package="5 mm [THT]"]
  R2 = Resistor [tolerance=±5% resistance=10k package=THT]
  R3 = Resistor [tolerance=±5% resistance=10k package=THT]
  S1 = Pushbutton [package="[THT]"]
  S2 = Pushbutton [package="[THT]"]
  R4 = Resistor [tolerance=±5% resistance=220 package=THT]
  R5 = Resistor [tolerance=±5% resistance=220 package=THT]
  J1 = Basic Servo
  hc-sr1 = hc-sr04

nets:
  N1: Componente1.D9_PWM, J1.pulse
  N2: Componente1.D10_PWM/SS, hc-sr1.Trig
  N3: Componente1.D11_PWM/MOSI, hc-sr1.Echo
  N4: Componente1.D12/MISO, R3.Pin_0, S1.Pin_3, S1.Pin_4
  N5: Componente1.D13/SCK, R2.Pin_0, S2.Pin_1, S2.Pin_2
  N6: Componente1.D3_PWM, R4.Pin_1
  N7: Componente1.D5_PWM, R5.Pin_1
  VCC: Componente1.5V, S1.Pin_1, S1.Pin_2, S2.Pin_3, S2.Pin_4, J1.vcc, hc-sr1.VCC
  GND: Componente1.GND, LED1.cathode, LED2.cathode, R2.Pin_1, R3.Pin_1, J1.gnd, hc-sr1.GND
  N8: LED1.anode, R4.Pin_0
  N9: LED2.anode, R5.Pin_0
